# Fritzing sketch RCar (saved by Fritzing 0.9.3b)
breadboards: 1

parts:
  Arduino_Nano = Arduino Nano (Rev3.0) (ICSP)
  LED = LED - 3mm [color="Yellow (595nm)" package="3 mm [THT]"]
  LED_2 = LED - 3mm [color="Yellow (595nm)" package="3 mm [THT]"]
  LED_3 = LED - 3mm [color="White (6500K)" package="3 mm [THT]"]
  LEDs = LED - 3mm [color="White (6500K)" package="3 mm [THT]"]
  LED2 = LED - 3mm [color="Red (633nm)" package="3 mm [THT]"]
  LED_4 = LED - 3mm [color="Red (633nm)" package="3 mm [THT]"]
  Micro_Servo_SG90 = Basic Servo
  Bluetooth_HC-05_Module = Bluetooth HC-05 Macho
  9V_Battery_&_Adapter = BC9VPC [package=bc9vpc]
  L298N_Motor_Driver = Arduino Motor Shield
  GPS_Module_(NEO-6M-0-001) = SUP500F [package=sup500f]
  Piezoelectric_Speaker = Piezo Speaker  # not connected
  DC_3V_Motor = DC Motor
  R1 = Resistor [tolerance=±5% resistance=220 package="1206 [SMD]"]
  R2 = Resistor [tolerance=±5% resistance=220 package="1206 [SMD]"]
  R3 = Resistor [tolerance=±5% resistance=220 package="1206 [SMD]"]
  R4 = Resistor [tolerance=±5% resistance=220 package="1206 [SMD]"]

nets:
  N1: Arduino_Nano.D1/TX, Bluetooth_HC-05_Module.RXD
  N2: Arduino_Nano.D0/RX, Bluetooth_HC-05_Module.TXD
  GND: Arduino_Nano.GND, LED.cathode, LED_2.cathode, LED_3.cathode, LEDs.cathode, LED2.cathode, LED_4.cathode, Micro_Servo_SG90.gnd, Bluetooth_HC-05_Module.GND, 9V_Battery_&_Adapter.V-, L298N_Motor_Driver.GND, GPS_Module_(NEO-6M-0-001).GND
  N3: Arduino_Nano.D2, R2.Pin_1
  N4: Arduino_Nano.D3, R1.Pin_1
  N5: Arduino_Nano.D5, R3.Pin_1
  N6: Arduino_Nano.D6, Micro_Servo_SG90.pulse
  N7: Arduino_Nano.D7, R4.Pin_1
  N8: Arduino_Nano.D9, L298N_Motor_Driver.D12
  N9: Arduino_Nano.D11/MOSI, L298N_Motor_Driver.D3
  N10: Arduino_Nano.D12/MISO, GPS_Module_(NEO-6M-0-001).TX-O
  VCC: Arduino_Nano.VIN, Micro_Servo_SG90.vcc, Bluetooth_HC-05_Module.VCC, L298N_Motor_Driver.5V, GPS_Module_(NEO-6M-0-001).VCC
  N11: Arduino_Nano.D13/SCK, GPS_Module_(NEO-6M-0-001).RX-I
  N12: LED.anode, R1.Pin_0
  N13: LED_2.anode, R2.Pin_0
  N14: LED_3.anode, LEDs.anode, R3.Pin_0
  N15: LED2.anode, LED_4.anode, R4.Pin_0
  N16: 9V_Battery_&_Adapter.V+, L298N_Motor_Driver.VIN
  N17: L298N_Motor_Driver.OUT2, DC_3V_Motor.pin_1
  N18: L298N_Motor_Driver.OUT1, DC_3V_Motor.pin_2
